// Logisim project LomannLecoq Groupe2.circ as structural Verilog: 3 circuits, main circuit main
// A
module main (
  input  C0,
  input  P0,
  input  G0,
  input  P1,
  input  G1,
  input  P2,
  input  G2,
  input  P3,
  input  G3,
  input  P4,
  input  G4,
  input  [3:0] B,
  input  [3:0] A,
  output C1,
  output C2,
  output C3,
  output C4,
  output [3:0] S
);

  wire and_1_out, and_2_out;

  Add1 add1_1 (.A(B[0]), .S(S[0]), .B(A[0]), .C_int(1'b0));  // open: G, P
  or or_1 (C1, G0, and_1_out);
  and and_1 (and_1_out, P0, C0);
  and and_2 (and_2_out, C1, P1);
  or or_2 (C2, G1, and_2_out);
endmodule

module Add1 (
  input  A,
  input  B,
  input  C_int,
  output S,
  output G,
  output P
);

  wire xor_1_out;

  xor xor_1 (xor_1_out, A, B);
  and and_1 (G, B, A);
  or or_1 (P, G, xor_1_out);
  xor xor_2 (S, C_int, xor_1_out);
endmodule

module propa (
  input  Cin0,
  input  P0,
  input  G0,
  output Cout0
);

  wire and_1_out;

  and and_1 (and_1_out, P0, Cin0);
  or or_1 (Cout0, G0, and_1_out);
endmodule
